# Fritzing sketch openVentilator (saved by Fritzing 0.9.2b)

parts:
  Bauteil1 = Arduino Uno (Rev3)
  Q1 = NPN-Transistor [package="TO92 [THT]"]
  Q2 = LTR-301 [package=ltr-301]
  LCD2 = LCD screen
  U1 = POT [package=pot_mammoth]
  LCM1602_IIC2 = LCM1602 IIC [part_number="LCM1602 IIC" chip_label="LCM1602 IIC" package="DIP (Dual Inline) [THT]"]
  U2 = POT [package=pot_mammoth]
  U3 = POT [package=pot_mammoth]

nets:
  N1: Bauteil1.A0, U1.S
  N2: Bauteil1.A1, U2.S
  N3: Bauteil1.A2, U3.S
  GND: Bauteil1.GND, Q1.E, U1.A, LCM1602_IIC2.GND, U2.A, U3.A
  N4: Bauteil1.D2, Q1.C
  5V: Bauteil1.5V, Q2.C, U1.E, LCM1602_IIC2.VCC, U2.E, U3.E
  N5: Q1.B, Q2.E
  VSS: LCD2.VSS, LCM1602_IIC2.VSS
  VDD: LCD2.VDD, LCM1602_IIC2.VDD
  N6: LCD2.V0, LCM1602_IIC2.V0
  N7: LCD2.RS, LCM1602_IIC2.RS
  N8: LCD2.R/W, LCM1602_IIC2.RW
  N9: LCD2.E, LCM1602_IIC2.E
  N10: LCD2.DB0, LCM1602_IIC2.D0
  N11: LCD2.DB1, LCM1602_IIC2.D1
  N12: LCD2.DB2, LCM1602_IIC2.D2
  N13: LCD2.DB3, LCM1602_IIC2.D3
  N14: LCD2.DB4, LCM1602_IIC2.D4
  N15: LCD2.DB5, LCM1602_IIC2.D5
  N16: LCD2.DB6, LCM1602_IIC2.D6
  N17: LCD2.DB7, LCM1602_IIC2.D7
  N18: LCD2.LED+, LCM1602_IIC2.A
  N19: LCD2.LED-, LCM1602_IIC2.K

custom parts:
  LCM1602 IIC: I2C-Module to use a 1602 or 2004 LCD on with the wire.h libory Serial LCD Modul
